// Logisim project control-logic.circ as structural Verilog: 1 circuit, main circuit control_logic
module control_logic (
  input  [31:0] Instruction,
  input  BrEq,
  input  BrLt,
  output PCSel,
  output RegWEn,
  output [2:0] ImmSel,
  output BrUn,
  output ASel,
  output BSel,
  output [3:0] ALUSel,
  output MemWEn,
  output [1:0] WBSel
);

  wire add000, and111, comparator_5_eq, comparator_8_eq, demultiplexer_2_out0, demultiplexer_2_out1,
       demultiplexer_2_out3, demultiplexer_2_out5, demultiplexer_4_out0, mul000, mulh, mulhu, or110,
       priority_encoder_1_p6, priority_encoder_1_p7, priority_encoder_1_p8, priority_encoder_1_p9,
       priority_encoder_1_p10, priority_encoder_1_p11, priority_encoder_1_p12, priority_encoder_1_p13,
       sll001, slt010, sra101, srl101, sub001, xor100;
  wire [5:0] priority_encoder_1_p14;
  wire [15:14] rom_1_data;

  ROM #(.addrWidth(6), .dataWidth(16)) rom_1 (
    .addr(priority_encoder_1_p14),
    .data({rom_1_data, WBSel, MemWEn, ALUSel, BSel, ASel, BrUn, ImmSel, RegWEn}));
  // Priority_Encoder #(.select_enc(6)) priority_encoder_1: pin names not known; wires that end beside it: xor100, srl101, sra101, or110, and111, priority_encoder_1_p6, priority_encoder_1_p7, priority_encoder_1_p8, priority_encoder_1_p9, priority_encoder_1_p10, priority_encoder_1_p11, priority_encoder_1_p12, priority_encoder_1_p13, priority_encoder_1_p14
  Comparator #(.mode("unsigned"), .width(10)) comparator_1 (
    .a(10'h13), .b({Instruction[14:12], Instruction[6:0]}), .eq(priority_encoder_1_p6));  // open: gt, lt
  Comparator #(.mode("unsigned"), .width(10)) comparator_2 (
    .a(10'h93), .b({Instruction[14:12], Instruction[6:0]}), .eq(priority_encoder_1_p7));  // open: gt, lt
  Comparator #(.mode("unsigned"), .width(10)) comparator_3 (
    .a(10'h113), .b({Instruction[14:12], Instruction[6:0]}), .eq(priority_encoder_1_p8));  // open: gt, lt
  Comparator #(.mode("unsigned"), .width(10)) comparator_4 (
    .a(10'h213), .b({Instruction[14:12], Instruction[6:0]}), .eq(priority_encoder_1_p9));  // open: gt, lt
  Demultiplexer demultiplexer_1 (
    .out0(priority_encoder_1_p10), .out1(priority_encoder_1_p11), .in(comparator_5_eq), .sel(Instruction[30]));
  Comparator #(.mode("unsigned"), .width(10)) comparator_5 (
    .a(10'h293), .b({Instruction[14:12], Instruction[6:0]}), .eq(comparator_5_eq));  // open: gt, lt
  Comparator #(.mode("unsigned"), .width(10)) comparator_6 (
    .a(10'h313), .b({Instruction[14:12], Instruction[6:0]}), .eq(priority_encoder_1_p12));  // open: gt, lt
  Comparator #(.mode("unsigned"), .width(10)) comparator_7 (
    .a(10'h393), .b({Instruction[14:12], Instruction[6:0]}), .eq(priority_encoder_1_p13));  // open: gt, lt
  Demultiplexer #(.select(3)) demultiplexer_2 (
    .out0(demultiplexer_2_out0), .out1(demultiplexer_2_out1), .out2(slt010), .out3(demultiplexer_2_out3),
    .out4(xor100), .out5(demultiplexer_2_out5), .out6(or110), .out7(and111), .in(comparator_8_eq),
    .sel(Instruction[14:12]));
  Comparator #(.mode("unsigned"), .width(7)) comparator_8 (
    .a(7'b0110011), .b(Instruction[6:0]), .eq(comparator_8_eq));  // open: gt, lt
  Demultiplexer demultiplexer_3 (.out0(add000), .out1(mul000), .in(demultiplexer_4_out0), .sel(Instruction[25]));
  Demultiplexer demultiplexer_4 (
    .out0(demultiplexer_4_out0), .out1(sub001), .in(demultiplexer_2_out0), .sel(Instruction[30]));
  Demultiplexer demultiplexer_5 (.out0(sll001), .out1(mulh), .in(demultiplexer_2_out1), .sel(Instruction[25]));
  Demultiplexer demultiplexer_6 (.out1(mulhu), .in(demultiplexer_2_out3), .sel(Instruction[25]));  // open: out0
  Demultiplexer demultiplexer_7 (.out0(srl101), .out1(sra101), .in(demultiplexer_2_out5), .sel(Instruction[30]));

  assign PCSel = 1'b0;

  // Other names for the same wires on the sheet: opcode[6:0] = Instruction[6:0]; funct3[2:0] = Instruction[14:12];
  //   funct7[6:0] = Instruction[31:25]

  // Notes on the sheet:
  //   INPUTS to your circuit
  //   Connect ROM Input here ->
  //   contents of rom_1 (hex, n*v repeats v):
  //   1001 1401 1601 1081 1481 1581 1101 1201 1281 1681 1301 1381 41 41 41 1041 10c3 1141 1241 12c3 16c3
  //   1341 13c1 844 844 844
  //   I and I* control
  //   ROM FOR CONTROL LOGIC
  //   DON'T CHANGE THE LOCATIONS OF THE INPUTS AND OUTPUTS!
  //   This is only if you choose to do the ROM option
  //   OUTPUT from your circuit
  //   Reminder: If using ROM, use combinational logic for PCSel
endmodule
